# Fritzing sketch wiring (saved by Fritzing 0.8.7b)
breadboards: 1

parts:
  U1 = Wemos Lolin D32
  U2 = WS2812 RGB LED strip
  Power_plug1 = Power plug
  R1 = Resistor [tolerance=±5% resistance=470 package=THT]
  C1 = Electrolytic Capacitor [capacitance=1000μF package="1010 [SMD, electrolytic]"]

nets:
  N1: U1.pin_6, R1.Pin_0
  VCC: U1.pin_14, U2.VCC, Power_plug1.VCC, C1.+
  N2: U1.pin_16, U1.pin_17
  GND: U1.pin_18, U1.pin_33, U2.GND, Power_plug1.GND, C1.-
  N3: U2.DIN, R1.Pin_1

custom parts:
  Wemos Lolin D32: Wemos Lolin D32 wifi and blue tooth board based on the ESP-32 cpu, digital I/Os 22, analog inputs 6, analog outputs 2 clock 240mhz, Flash 4Mbytes, lipo battery charger (500ma connection broken out on breadboard but not pcb), usb. The mounting holes are only set on the silkscreen, if you want actual holes in the pcb copy the hole from the pcb menu in parts over the top of the hole in the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
  WS2812 RGB LED strip: WS2812 strip
